# Fritzing sketch Base station (saved by Fritzing 0.9.10b)
breadboards: 1

parts:
  Mod1 = Amica NodeMCU DEVKIT 1.0
  Part2 = BH1750
  Grove1 = Grove OLED 128x96
  S1 = Pushbutton [package="[THT]"]
  HC-SR04_Sensor_1 = HC-SR04 Ultrasonic Distance Sensor
  R1 = Resistor [tolerance=±5% power=0.25 resistance=10k package=THT]
  M1 = BME280

nets:
  VCC: Mod1.pin1, Mod1.pin_10, Mod1.pin_26, Part2.VCC, S1.Pin_1, S1.Pin_2, HC-SR04_Sensor_1.VCC, M1.VIN
  GND: Mod1.pin2, Mod1.pin_9, Mod1.pin_25, Mod1.pin_29, Part2.GND, HC-SR04_Sensor_1.GND, R1.Pin_0, M1.GND
  N1: Mod1.pin6, HC-SR04_Sensor_1.ECHO
  N2: Mod1.pin7, HC-SR04_Sensor_1.TRIG
  N3: Mod1.pin8, S1.Pin_3, S1.Pin_4, R1.Pin_1
  N4: Mod1.pin_13, Part2.SDA, Grove1.SDA, M1.SDA
  N5: Mod1.pin_14, Part2.SCL, Grove1.SCL, M1.SCL

custom parts:
  BH1750: Light Sensor
  BME280: Temperature Humidity Barometric presure Sensor
